# Fritzing sketch SmartShifter (saved by Fritzing 0.8.7b)

parts:
  Part1 = Arduino Nano (Rev3.0) (ICSP)
  DI1 = 7-Segment LED Display [package=THT]
  S1 = Pushbutton [package="[THT]"]
  S2 = Pushbutton [package="[THT]"]
  S3 = Pushbutton [package="[THT]"]
  R1 = Resistor [tolerance=±5% resistance=220 package=THT]
  R2 = Resistor [tolerance=±5% resistance=220 package=THT]

nets:
  N1: Part1.D2, DI1.cathodeC
  N2: Part1.D3, DI1.cathodeD
  N3: Part1.D4, DI1.cathodeE
  N4: Part1.D5, DI1.cathodeB
  N5: Part1.D6, DI1.cathodeA
  N6: Part1.D7, DI1.cathodeF
  N7: Part1.D8, DI1.cathodeG
  N8: Part1.D10, S3.Pin_2
  N9: Part1.D11/MOSI, S2.Pin_1, S2.Pin_2
  N10: Part1.D12/MISO, S1.Pin_1, S1.Pin_2
  N11: Part1.GND, S2.Pin_3, S2.Pin_4, S3.Pin_3, S3.Pin_4
  N12: DI1.commAnode#2, R2.Pin_1
  N13: DI1.commAnode#7, R1.Pin_1
  N14: R1.Pin_0, R2.Pin_0

notes:
  Top = Gear Up
  Middle = Gear Down
  Bottom = Reset
  External Power
